# Fritzing sketch Schemat (saved by Fritzing 0.9.3b)

parts:
  Part1 = Arduino Nano (Rev3.0)
  LCD1 = LCD screen
  ANT1 = Antenna
  LED1 = LED - 5mm [color="Green (570nm)" package="5 mm [THT]"]
  LED2 = LED - 5mm [color="Red (633nm)" package="5 mm [THT]"]
  S1 = Pushbutton [package="[THT]"]
  S2 = Pushbutton [package="[THT]"]
  J1 = Piezo Speaker

nets:
  N1: Part1.D5, ANT1.antenna_lead
  N2: Part1.D6, S1.Pin_2
  N3: Part1.D7, S2.Pin_1, S2.Pin_2
  N4: Part1.D8, LED1.anode
  N5: Part1.D9, LED2.anode
  N6: Part1.D10, J1.pin2
  N7: Part1.A5, LCD1.VDD
  N8: Part1.A4, LCD1.VSS

notes:
  scl
  Odbiornik podczerwieni
  zielony
  czerwony
